// Logisim project TallerLogica-Combinatorios.circ as structural Verilog: 11 circuits, main circuit sumador_simple
module sumador_simple (
  input  A,
  input  B,
  output S,
  output Cout
);

  xor xor_1 (S, A, B);
  and and_1 (Cout, A, B);
endmodule

module sumador_completo (
  input  Cin,
  input  A,
  input  B,
  output S,
  output Cout
);

  wire sumador_simple_1_cout, sumador_simple_2_cout, sumador_simple_2_s;

  sumador_simple sumador_simple_1 (.A(Cin), .B(sumador_simple_2_s), .S(S), .Cout(sumador_simple_1_cout));
  sumador_simple sumador_simple_2 (.A(A), .B(B), .S(sumador_simple_2_s), .Cout(sumador_simple_2_cout));
  or or_1 (Cout, sumador_simple_1_cout, sumador_simple_2_cout);
endmodule

module sumador_4 (
  input  Cin,
  input  [3:0] A,
  input  [3:0] B,
  output [3:0] S,
  output Cout
);

  wire sumador_completo_1_cout, sumador_completo_2_cout, sumador_completo_3_cout;

  sumador_completo sumador_completo_1 (.Cin(Cin), .A(A[0]), .B(B[0]), .S(S[0]), .Cout(sumador_completo_1_cout));
  sumador_completo sumador_completo_2 (
    .Cin(sumador_completo_1_cout), .A(A[1]), .B(B[1]), .S(S[1]), .Cout(sumador_completo_2_cout));
  sumador_completo sumador_completo_3 (
    .Cin(sumador_completo_2_cout), .A(A[2]), .B(B[2]), .S(S[2]), .Cout(sumador_completo_3_cout));
  sumador_completo sumador_completo_4 (.Cin(sumador_completo_3_cout), .A(A[3]), .B(B[3]), .S(S[3]), .Cout(Cout));
  Hex_Digit_Display hex_digit_display_1 (.value(S));  // open: dp
endmodule

module comparador_cero (
  input  [3:0] A,
  output Z
);

  wire and_1_out, and_2_out, not_1_out, not_2_out, not_3_out, not_4_out;

  not not_1 (not_1_out, A[0]);
  not not_2 (not_2_out, A[1]);
  not not_3 (not_3_out, A[2]);
  not not_4 (not_4_out, A[3]);
  and and_1 (and_1_out, not_1_out, not_2_out);
  and and_2 (and_2_out, not_3_out, not_4_out);
  and and_3 (Z, and_1_out, and_2_out);
endmodule

module sumador_flags (
  input  Cin,
  input  [3:0] A,
  input  [3:0] B,
  output [3:0] S,
  output N,
  output Z,
  output V,
  output C
);

  wire sumador_completo_1_cout, sumador_completo_2_cout, sumador_completo_3_cout;

  sumador_completo sumador_completo_1 (.Cin(Cin), .A(A[0]), .B(B[0]), .S(S[0]), .Cout(sumador_completo_1_cout));
  sumador_completo sumador_completo_2 (
    .Cin(sumador_completo_1_cout), .A(A[1]), .B(B[1]), .S(S[1]), .Cout(sumador_completo_2_cout));
  sumador_completo sumador_completo_3 (
    .Cin(sumador_completo_2_cout), .A(A[2]), .B(B[2]), .S(S[2]), .Cout(sumador_completo_3_cout));
  sumador_completo sumador_completo_4 (.Cin(sumador_completo_3_cout), .A(A[3]), .B(B[3]), .S(N), .Cout(C));
  xor xor_1 (V, sumador_completo_3_cout, C);
  Hex_Digit_Display hex_digit_display_1 (.value({N, S[2:0]}));  // open: dp
  comparador_cero comparador_cero_1 (.A({N, S[2:0]}), .Z(Z));

  assign S[3] = N;
endmodule

module incrementador_4 (
  input  [3:0] A,
  output [3:0] S
);

  wire sumador_4_1_cout;

  sumador_4 sumador_4_1 (.Cin(1'b0), .A(A), .B(4'b0001), .S(S), .Cout(sumador_4_1_cout));
  Hex_Digit_Display hex_digit_display_1 (.value(S));  // open: dp
  // also tied to GND on the sheet: sumador_4_1_cout
endmodule

module inversor_4 (
  input  [3:0] A,
  input  INV,
  output [3:0] S
);

  wire [3:0] incrementador_4_1_s, not_4_out;

  not not_1 (not_4_out[3], A[3]);
  not not_2 (not_4_out[2], A[2]);
  not not_3 (not_4_out[1], A[1]);
  not not_4 (not_4_out[0], A[0]);
  incrementador_4 incrementador_4_1 (.A(not_4_out), .S(incrementador_4_1_s));
  Multiplexer #(.width(4)) multiplexer_1 (.in0(A), .in1(incrementador_4_1_s), .out(S), .sel(INV));
  Hex_Digit_Display hex_digit_display_1 (.value(S));  // open: dp
endmodule

module ALU (
  input  [3:0] A,
  input  [3:0] B,
  input  [1:0] OP,
  output [3:0] out_4,
  output N,
  output Z,
  output [3:0] out_7,
  output V,
  output C,
  output [3:0] S,
  output [3:0] out_11,
  output [3:0] out_12
);

  wire [3:0] inversor_4_1_s;

  and and_1 (out_11[0], A[0], B[0]);
  and and_2 (out_11[1], A[1], B[1]);
  and and_3 (out_11[2], A[2], B[2]);
  and and_4 (out_11[3], A[3], B[3]);
  or or_1 (out_12[0], B[0], A[0]);
  or or_2 (out_12[1], A[1], B[1]);
  or or_3 (out_12[2], B[2], A[2]);
  or or_4 (out_12[3], A[3], B[3]);
  sumador_flags sumador_flags_1 (.A(A), .B(B), .S(out_4), .N(N), .Z(Z), .V(V), .C(C));  // open: Cin
  inversor_4 inversor_4_1 (.A(B), .INV(1'b1), .S(inversor_4_1_s));
  sumador_flags sumador_flags_2 (.A(A), .B(inversor_4_1_s), .S(out_7));  // open: Cin, N, Z, V, C
  Multiplexer #(.select(2), .width(4)) multiplexer_1 (
    .in0(out_4), .in1(out_7), .in2(out_11), .in3(out_12), .out(S), .sel(OP));
  Hex_Digit_Display hex_digit_display_1 (.value(S));  // open: dp
endmodule

module verificador (
  output [3:0] out_1,
  output [3:0] out_2,
  output [1:0] out_3,
  output halt,
  output N,
  output Z,
  output V,
  output C,
  output [3:0] res
);

  wire clock_1_out;

  Clock clock_1 (.out(clock_1_out));
  Counter #(.max('h3ff), .width(10)) counter_1 (
    .clk(clock_1_out), .carry(halt), .Q({out_3, out_2, out_1}));  // open: clr, load, up, count, D
  // ALU alu_1: pin names not known; wires that end beside it: out_1, out_2, out_3, N, Z, V, C, res
endmodule

module ALU_v2 (
  input  Cin,
  input  in_2,
  input  [3:0] B,
  input  [3:0] A,
  input  [1:0] OP,
  output N,
  output Z,
  output V,
  output C,
  output [3:0] S,
  output [3:0] out_11,
  output [3:0] out_12
);

  wire SUMA_PARA_RESTAR_c, SUMA_PARA_RESTAR_n, SUMA_PARA_RESTAR_v, SUMA_PARA_RESTAR_z, SUMADOR_c, SUMADOR_n,
       SUMADOR_v, SUMADOR_z;
  wire [3:0] inversor_4_1_s, INVERSOR_RESTA_s, SUMA_PARA_RESTAR_s, SUMADOR_s;

  Hex_Digit_Display hex_digit_display_1 (.value(B));  // open: dp
  Hex_Digit_Display hex_digit_display_2 (.value(A));  // open: dp
  and and_1 (out_11[0], A[0], B[0]);
  and and_2 (out_11[1], A[1], B[1]);
  and and_3 (out_11[2], A[2], B[2]);
  and and_4 (out_11[3], A[3], B[3]);
  or or_1 (out_12[0], A[0], B[0]);
  or or_2 (out_12[1], A[1], B[1]);
  or or_3 (out_12[2], A[2], B[2]);
  or or_4 (out_12[3], A[3], B[3]);
  inversor_4 INVERSOR_RESTA (.A(B), .INV(1'b1), .S(INVERSOR_RESTA_s));
  sumador_flags SUMADOR (
    .Cin(Cin), .A(A), .B(B), .S(SUMADOR_s), .N(SUMADOR_n), .Z(SUMADOR_z), .V(SUMADOR_v), .C(SUMADOR_c));
  sumador_flags SUMA_PARA_RESTAR (
    .Cin(in_2), .A(A), .B(INVERSOR_RESTA_s), .S(SUMA_PARA_RESTAR_s), .N(SUMA_PARA_RESTAR_n),
    .Z(SUMA_PARA_RESTAR_z), .V(SUMA_PARA_RESTAR_v), .C(SUMA_PARA_RESTAR_c));
  inversor_4 inversor_4_1 (.A(SUMA_PARA_RESTAR_s), .INV(1'b1), .S(inversor_4_1_s));
  Multiplexer #(.select(2), .width(4)) multiplexer_1 (
    .in0(SUMADOR_s), .in1(inversor_4_1_s), .in2(out_11), .in3(out_12), .out(S), .sel(OP));
  Multiplexer multiplexer_2 (.in0(SUMADOR_n), .in1(SUMA_PARA_RESTAR_n), .out(N), .sel(OP[0]));
  Multiplexer multiplexer_3 (.in0(SUMADOR_z), .in1(SUMA_PARA_RESTAR_z), .out(Z), .sel(OP[0]));
  Multiplexer multiplexer_4 (.in0(SUMADOR_v), .in1(SUMA_PARA_RESTAR_v), .out(V), .sel(OP[0]));
  Multiplexer multiplexer_5 (.in0(SUMADOR_c), .in1(SUMA_PARA_RESTAR_c), .out(C), .sel(OP[0]));
  Hex_Digit_Display hex_digit_display_3 (.value(S));  // open: dp
endmodule

module RESTADOR (
  input  [3:0] A,
  input  [3:0] B,
  output [3:0] S,
  output N,
  output Z,
  output V,
  output C
);

  Hex_Digit_Display hex_digit_display_1 (.value(A));  // open: dp
  Hex_Digit_Display hex_digit_display_2 (.value(B));  // open: dp
  Hex_Digit_Display hex_digit_display_3 (.value(S));  // open: dp
endmodule
